// Logisim project IICT.circ as structural Verilog: 1 circuit, main circuit main
module main (
  input  C,
  input  D,
  input  E,
  input  F,
  input  G,
  output out_6
);

  wire C_D_out, CG_out, E_F_out;

  and C_D (C_D_out, C, D);
  and E_F (E_F_out, E, F);
  and CG (CG_out, C, G);
  or CD_EF_CG (out_6, C_D_out, E_F_out, CG_out);
endmodule
