// Logisim project eighth.circ as structural Verilog: 1 circuit, main circuit main
module main (
  input  A,
  input  B,
  output out_3,
  output out_4
);

  wire not_1_out, not_2_out;

  not not_1 (not_1_out, B);
  not not_2 (not_2_out, A);
  nand nand_1 (out_3, A, B);
  or or_1 (out_4, not_1_out, not_2_out);
endmodule
