// Logisim project fifth.circ as structural Verilog: 1 circuit, main circuit main
module main (
  input  A,
  input  B,
  input  C,
  input  D,
  output out_5
);

  wire nand_1_out, nor_1_out, xnor_1_out;

  xnor xnor_1 (xnor_1_out, A, B);
  nand nand_1 (nand_1_out, C, D);
  nor nor_1 (nor_1_out, B, D);
  or or_1 (out_5, xnor_1_out, nor_1_out, nand_1_out);
endmodule
