// Logisim project first.circ as structural Verilog: 1 circuit, main circuit main
module main (
  input  A,
  input  B,
  input  C,
  input  D,
  output out_5
);

  wire nand_1_out, not_1_out, not_2_out, or_1_out, or_2_out;

  or or_1 (or_1_out, A, C);
  nand nand_1 (nand_1_out, A, D);
  not not_1 (not_1_out, B);
  not not_2 (not_2_out, C);
  or or_2 (or_2_out, not_1_out, not_2_out);
  and and_1 (out_5, or_1_out, nand_1_out, or_2_out);
endmodule
