// Logisim project fourth.circ as structural Verilog: 1 circuit, main circuit main
module main (
  input  A,
  input  B,
  input  C,
  input  D,
  output out_5
);

  wire and_1_out, and_2_out, and_3_out, and_4_out, nor_1_out, not_1_out, xnor_1_out;

  not not_1 (not_1_out, C);
  xnor xnor_1 (xnor_1_out, D, D);
  and and_1 (and_1_out, A, B, not_1_out);
  and and_2 (and_2_out, A, C, D);
  and and_3 (and_3_out, and_1_out, xnor_1_out);
  nor nor_1 (nor_1_out, A, B, C);
  and and_4 (and_4_out, nor_1_out, and_2_out);
  or or_1 (out_5, and_3_out, and_4_out);
endmodule
