// Logisim project ninth.circ as structural Verilog: 1 circuit, main circuit main
module main (
  input  A,
  input  B,
  input  C,
  output out_4,
  output out_5
);

  wire and_2_out, and_3_out, or_1_out;

  or or_1 (or_1_out, B, C);
  and and_1 (out_4, A, or_1_out);
  and and_2 (and_2_out, A, B);
  and and_3 (and_3_out, A, C);
  or or_2 (out_5, and_2_out, and_3_out);
endmodule
