// Logisim project second.circ as structural Verilog: 1 circuit, main circuit main
module main (
  input  A,
  input  B,
  input  C,
  input  D_minus,
  output out_5
);

  wire and_1_out, nand_1_out, not_1_out;

  not not_1 (not_1_out, A);
  and and_1 (and_1_out, not_1_out, A);
  nand nand_1 (nand_1_out, B, C, D_minus);
  or or_1 (out_5, and_1_out, nand_1_out);
endmodule
