// Logisim project seventh.circ as structural Verilog: 1 circuit, main circuit main
module main (
  input  A,
  input  B,
  output out_3,
  output out_4
);

  wire or_1_out;

  or or_1 (or_1_out, A, B);
  and and_1 (out_3, A, or_1_out);

  assign out_4 = A;
endmodule
