// Logisim project sixth.circ as structural Verilog: 1 circuit, main circuit main
module main (
  input  A,
  input  B,
  input  C,
  input  D,
  output out_5
);

  wire nor_1_out, or_1_out, xor_1_out;

  or or_1 (or_1_out, A, B);
  nor nor_1 (nor_1_out, A, C);
  xor xor_1 (xor_1_out, B, D);
  and and_1 (out_5, or_1_out, nor_1_out, xor_1_out);
endmodule
