// Logisim project tenth.circ as structural Verilog: 1 circuit, main circuit main
module main (
  input  A,
  input  B,
  input  C,
  output out_4,
  output out_5
);

  wire and_1_out, and_3_out;

  and and_1 (and_1_out, A, B);
  and and_2 (out_4, and_1_out, C);
  and and_3 (and_3_out, B, C);
  and and_4 (out_5, A, and_3_out);
endmodule
