// Logisim project third.circ as structural Verilog: 1 circuit, main circuit main
module main (
  input  A,
  input  B,
  input  C,
  input  D,
  output out_5
);

  wire xnor_1_out, xnor_2_out, xnor_3_out;

  xnor xnor_1 (xnor_1_out, A, B);
  xnor xnor_2 (xnor_2_out, B, C);
  xnor xnor_3 (xnor_3_out, C, D);
  and and_1 (out_5, xnor_1_out, xnor_2_out, xnor_3_out);
endmodule
